# Fritzing sketch Stripboard_49x18 (saved by Fritzing 0.9.6b)
stripboards: 1

parts:
  J3 = male pin header, 2 pins [form="♂ (male)"]
  R1 = Resistor [tolerance=±5% power=0.25 resistance=2.2k package=THT]
  D1 = Rectifier Diode [part_number=1N4001 package="300 mil [THT]"]
  D2 = Rectifier Diode [part_number=1N4001 package="300 mil [THT]"]
  R2 = Resistor [tolerance=±5% power=0.25 resistance=10 package=THT]
  Q1 = PNP-Transistor [package="TO92 [THT]"]
  J4 = male pin header, 4 pins [form="♂ (male)"]
  U1 = Optocoupler [package=THT]
  D4 = Rectifier Diode [part_number=1N4148 package="300 mil [THT]"]
  LED1 = LED - 5mm [color="Red (633nm)" current=0.030 package="5 mm [THT]"]
  R3 = Resistor [tolerance=±5% power=0.25 resistance=1.5k package=THT]
  J5 = male pin header, 4 pins [form="♂ (male)"]
  J6 = male pin header, 4 pins [form="♂ (male)"]
  J7 = male pin header, 4 pins [form="♂ (male)"]
  R4 = Resistor [tolerance=±5% power=0.25 resistance=220 package=THT]
  LED2 = LED - 5mm [color="Red (633nm)" current=0.030 package="5 mm [THT]"]
  C1 = Ceramic Capacitor [capacitance=100nF voltage=35V package="100 mil [THT, multilayer]"]
  R5 = Resistor [tolerance=±5% power=0.25 resistance=220 package=THT]

nets:
  N1: J3.pin1, J3.pin2, R1.Pin_0
  N2: R1.Pin_1, D1.anode, D2.cathode, R2.Pin_0
  N3: D1.cathode, D2.anode, Q1.E, J5.pin1, J5.pin2, J5.pin3, J5.pin4
  N4: R2.Pin_1, Q1.B
  N5: Q1.C, D4.anode, R5.Pin_0
  N6: J4.pin1, J4.pin2, J4.pin3, J4.pin4, U1.Pin_2, C1.1, R5.Pin_1
  N7: U1.Pin_1, LED1.cathode
  N8: U1.Pin_4, J6.pin1, J6.pin2, J6.pin3, J6.pin4
  N9: U1.Pin_5, R4.Pin_1
  N10: D4.cathode, R3.Pin_0, C1.0
  N11: LED1.anode, R3.Pin_1
  N12: J7.pin1, J7.pin2, J7.pin3, J7.pin4, LED2.anode
  N13: R4.Pin_0, LED2.cathode
